# Fritzing sketch controller (saved by Fritzing 0.9.2b)
circuit board: 8.46667cm x 5.64444cm
breadboards: 1

parts:
  Part1 = Arduino Nano (Rev3.0)
  BTN_R_Fast/Slow = Round Pushbutton
  24v_120w_DC_Scooter_Motor = DC Motor
  U2 = L298 [package=multiwatt15]
  BTN_L_Stop/Start = Round Pushbutton
  R1 = Resistor [tolerance=±5% resistance=1k package=THT]
  R2 = Resistor [tolerance=±5% resistance=1k package=THT]
  J1 = 3.5mm Audio Jack [package=audio-jack-3.5mm-smd]
  J2 = 3.5mm Audio Jack [package=audio-jack-3.5mm-smd]

nets:
  N1: Part1.GND, R1.Pin_0
  N2: Part1.D9, U2.ENA
  N3: Part1.D11/MOSI, R2.Pin_1, J1.LEFT
  N4: Part1.D12/MISO, R1.Pin_1, J1.RIGHT
  N5: Part1.5V, J1.SLEEVE
  N6: BTN_R_Fast/Slow.leg0, BTN_L_Stop/Start.leg0, J2.SLEEVE
  N7: BTN_R_Fast/Slow.leg1, J2.RIGHT
  N8: 24v_120w_DC_Scooter_Motor.pin_1, U2.OUT1
  N9: 24v_120w_DC_Scooter_Motor.pin_2, U2.OUT2
  13.5V: U2.VS
  N10: U2.IN2, U2.VLS
  GND: U2.GND, R2.Pin_0
  N11: BTN_L_Stop/Start.leg1, J2.LEFT

notes:
  mini-leslie v1, https://github.com/dizzib/mini-leslie, 1.0

// code stored in the sketch: controller.ino
const int PIN_ENA    = 9;
const int PIN_BTN_L  = 11;
const int PIN_BTN_R  = 12;
const int RAMP_DELAY = 30; // ms

// assumes 13.5V input
enum STATE { STOP = 0, SLOW = 146, FAST = 235 };

void setup() {
  Serial.begin(9600);

  pinMode(PIN_ENA,  OUTPUT);
  pinMode(PIN_BTN_L, INPUT);
  pinMode(PIN_BTN_R, INPUT);

  // increase pwm width from 490Hz to 30Khz to stop motor buzz
  // http://forum.arduino.cc/index.php/topic,16612.0.html#4
  // MAY HAVE SIDE EFFECTS!
  TCCR1B = TCCR1B & 0b11111000 | 0x01;
}

void loop() {
  static int state = STOP;
  static int speed = STOP;

  setState(&state);
  setSpeed(&state, &speed);
}

void setState(int *state) {
  bool btn_l = digitalRead(PIN_BTN_L);
  bool btn_r = digitalRead(PIN_BTN_R);
  *state = btn_l ? (btn_r ? FAST : SLOW) : STOP;
}

void setSpeed(int *state, int *speed) {
  const int KICKSTART = 5;
  if (*speed > SLOW) switch (*state) {
    case FAST:
      if (*speed < FAST) (*speed)++;
      break;
    default:
      if (*speed > SLOW) (*speed)--;
      break;
  }
  else switch (*state) {
    case FAST:
      *speed = SLOW + 1;
      break;
    case SLOW:
      *speed = SLOW + ((*speed == STOP) ? KICKSTART : 0);
      break;
    case STOP:
      *speed = STOP;
      break;
  }
  Serial.println(*speed);
  analogWrite(PIN_ENA, *speed);
  delay(RAMP_DELAY);
}
